# Fritzing sketch PN5180_RPi3 (saved by Fritzing 0.9.4)
circuit board: 8.53488cm x 5.63626cm
breadboards: 1

parts:
  Raspberry_Pi_1 = Raspberry Pi 3 [part_number=RPI-3-V1.2]
  PN5180-NFC = PN5180-NFC

nets:
  3V3: Raspberry_Pi_1.3v3, Raspberry_Pi_1.3V3, PN5180-NFC.3.3V
  N1: Raspberry_Pi_1.GIPO10, PN5180-NFC.MOSI
  N2: Raspberry_Pi_1.GIPO9, PN5180-NFC.MISO
  N3: Raspberry_Pi_1.GIPO11, PN5180-NFC.SCK
  N4: Raspberry_Pi_1.GIPO7, PN5180-NFC.RST
  N5: Raspberry_Pi_1.GIPO8, PN5180-NFC.NSS
  N6: Raspberry_Pi_1.GIPO25, PN5180-NFC.BUSY
  N7: Raspberry_Pi_1.GIPO23, PN5180-NFC.IRQ
  GND: Raspberry_Pi_1.GND, PN5180-NFC.GND, PN5180-NFC.AUX
  5V: Raspberry_Pi_1.5V, PN5180-NFC.5V

custom parts:
  PN5180-NFC: RFID High Frequency IC card reader/writer based on the PN5180 chip from NXP.
